// Logisim project CPU_simple.circ as structural Verilog: 9 circuits, main circuit main
module main (
  input  in_1,
  output [31:0] out_2,
  output out_3,
  output [4:0] out_4,
  output [31:0] out_5,
  output out_6,
  output [4:0] out_7,
  output [31:0] out_8
);

  wire ALUsrc, Clock, EXTop, MemtoReg, RegDst, Zero;
  wire [1:0] C;
  wire [3:0] TYPE;
  wire [15:0] Imm16;
  wire [25:0] Imm26;
  wire [31:0] D, ext_1_out_3, MemAddr, multiplexer_1_out, npc_1_npc, Num1, pc_1_pc;

  Clock clock_1 (.out(Clock));
  Bit_Extender #(.in_width(32)) bit_extender_1 (.in(out_2), .out(Imm16));
  Bit_Extender #(.in_width(32), .out_width(26)) bit_extender_2 (.in(out_2), .out(Imm26));
  PC pc_1 (.NPC(npc_1_npc), .CLK(Clock), .RESET(in_1), .PC(pc_1_pc));
  EXT ext_1 (.in_1(Imm16), .in_2(EXTop), .out_3(ext_1_out_3));
  NPC npc_1 (.PC(pc_1_pc), .Imm26(Imm26), .GRF(Num1), .Imm16(Imm16), .control(C), .zero(Zero), .NPC(npc_1_npc));
  IM im_1 (.in_1(pc_1_pc), .out_2(out_2));
  Multiplexer #(.width(32), .enable("false")) multiplexer_1 (
    .in0(out_8), .in1(ext_1_out_3), .out(multiplexer_1_out), .sel(ALUsrc));
  ALU alu_1 (
    .num1(Num1), .num2(multiplexer_1_out), .op(TYPE), .RESULT({MemAddr[31:7], out_7, MemAddr[1:0]}),
    .Zero(Zero));
  Controller controller_1 (
    .Op(out_2[31:26]), .funct(out_2[5:0]), .MemWrite(out_6), .RegWrite(out_3), .control(C), .out_8(TYPE),
    .RegDst(RegDst), .ESTop(EXTop), .ALUsrc(ALUsrc), .MemtoReg(MemtoReg));
  Multiplexer #(.width(5), .enable("false")) multiplexer_2 (
    .in0(out_2[20:16]), .in1(out_2[15:11]), .out(out_4), .sel(RegDst));
  GRF grf_1 (
    .A1(out_2[25:21]), .A2(out_2[20:16]), .A3(out_4), .WD(out_5), .RD1(Num1), .RD2(out_8), .clk(Clock),
    .reset(in_1), .we(out_3));
  Multiplexer #(.width(32), .enable("false")) multiplexer_3 (
    .in0({MemAddr[31:7], out_7, MemAddr[1:0]}), .in1(D), .out(out_5), .sel(MemtoReg));
  DM dm_1 (.in_1({MemAddr[31:7], out_7, MemAddr[1:0]}), .in_2(out_8), .out_6(D), .CLK(Clock), .in_5(in_1));  // open: WE
  Multiplexer multiplexer_4 ();  // open: in0, in1, out, sel, en

  // Other names for the same wires on the sheet: Funct[5:0] = out_2[5:0]; Instr[31:0] = out_2; A2[4:0] = out_2[20:16];
  //   A1[4:0] = out_2[25:21]; OP[5:0] = out_2[31:26]; MemAddr[6:2] = out_7; MemData[31:0] = out_8; MemWrite = out_6;
  //   RegAddr[4:0] = out_4; RegData[31:0] = out_5; RegWrite = out_3; RESET = in_1
endmodule

module PC (
  input  [31:0] NPC,
  input  CLK,
  input  RESET,
  output [31:0] PC
);

  wire [31:0] register_1_q, xor_1_out;

  assign xor_1_out = 32'h3000 ^ NPC;  // XOR_Gate xor_1, 32 bits wide
  Register #(.width(32)) register_1 (.D(xor_1_out), .Q(register_1_q), .clk(CLK), .clr(RESET));  // open: en
  assign PC = 32'h3000 ^ register_1_q;  // XOR_Gate xor_2, 32 bits wide
endmodule

module NPC (
  input  [31:0] PC,
  input  [25:0] Imm26,
  input  [31:0] GRF,
  input  [15:0] Imm16,
  input  [1:0] control,
  input  zero,
  output [31:0] NPC
);

  wire [31:0] adder_1_out, adder_2_out, bit_extender_1_out, multiplexer_1_out;

  Adder #(.width(32)) adder_1 (.a(32'h4), .b(PC), .out(adder_1_out));  // open: cin, cout
  assign bit_extender_1_out = {{14{Imm16[15]}}, {Imm16, 2'b00}};  // Bit_Extender bit_extender_1
  Adder #(.width(32)) adder_2 (.a(adder_1_out), .b(bit_extender_1_out), .out(adder_2_out));  // open: cin, cout
  Multiplexer #(.width(32), .enable("false")) multiplexer_1 (
    .in0(adder_1_out), .in1(adder_2_out), .out(multiplexer_1_out), .sel(zero));
  Multiplexer #(.select(2), .width(32), .enable("false")) multiplexer_2 (
    .in0(adder_1_out), .in1({PC[31:28], Imm26, 2'b00}), .in2(GRF), .in3(multiplexer_1_out), .out(NPC),
    .sel(control));
endmodule

module ALU (
  input  [31:0] num1,
  input  [31:0] num2,
  input  [3:0] op,
  output [31:0] RESULT,
  output Zero
);

  wire [31:0] adder_1_out, or_1_out, subtractor_1_out;

  Adder #(.width(32)) adder_1 (.a(num1), .b(num2), .out(adder_1_out));  // open: cin, cout
  assign or_1_out = num1 | num2;  // OR_Gate or_1, 32 bits wide
  Subtractor #(.width(32)) subtractor_1 (.a(num1), .b(num2), .out(subtractor_1_out));  // open: bin, bout
  Multiplexer #(.select(4), .width(32), .enable("false")) multiplexer_1 (
    .in0(adder_1_out), .in1(subtractor_1_out), .in2(adder_1_out), .in3(adder_1_out), .in4(or_1_out),
    .in7(adder_1_out), .out(RESULT), .sel(op));  // open: in5, in6, in8, in9, in10, in11, in12, in13, in14, in15
  Comparator #(.width(32)) comparator_1 (.a(subtractor_1_out), .b({32{1'b0}}), .eq(Zero));  // open: gt, lt
endmodule

module GRF (
  input  [4:0] A1,
  input  clk,
  input  reset,
  input  we,
  input  [4:0] A2,
  input  [4:0] A3,
  input  [31:0] WD,
  output [31:0] RD1,
  output [31:0] RD2
);

  wire [31:0] I0, I1, I2, I3, I4, I5, I6, I7, I8, I9, I10, I11, I12, I13, I14, I15, I16, I17, I18, I19, I20,
       I21, I22, I23, I24, I25, I26, I27, I28, I29, I30, I31, O0, O1, O2, O3, O4, O5, O6, O7, O8, O9, O10,
       O11, O12, O13, O14, O15, O16, O17, O18, O19, O20, O21, O22, O23, O24, O25, O26, O27, O28, O29, O30,
       O31;

  Demultiplexer #(.select(5), .width(32), .tristate("true")) demultiplexer_1 (
    .out0(I0), .out1(I1), .out2(I2), .out3(I3), .out4(I4), .out5(I5), .out6(I6), .out7(I7), .out8(I8),
    .out9(I9), .out10(I10), .out11(I11), .out12(I12), .out13(I13), .out14(I14), .out15(I15), .out16(I16),
    .out17(I17), .out18(I18), .out19(I19), .out20(I20), .out21(I21), .out22(I22), .out23(I23), .out24(I24),
    .out25(I25), .out26(I26), .out27(I27), .out28(I28), .out29(I29), .out30(I30), .out31(I31), .in(WD),
    .sel(A3));  // open: en
  Multiplexer #(.select(5), .width(32)) multiplexer_1 (
    .in0(O0), .in1(O1), .in2(O2), .in3(O3), .in4(O4), .in5(O5), .in6(O6), .in7(O7), .in8(O8), .in9(O9),
    .in10(O10), .in11(O11), .in12(O12), .in13(O13), .in14(O14), .in15(O15), .in16(O16), .in17(O17),
    .in18(O18), .in19(O19), .in20(O20), .in21(O21), .in22(O22), .in23(O23), .in24(O24), .in25(O25),
    .in26(O26), .in27(O27), .in28(O28), .in29(O29), .in30(O30), .in31(O31), .out(RD2), .sel(A2));  // open: en
  Multiplexer #(.select(5), .width(32)) multiplexer_2 (
    .in0(O0), .in1(O1), .in2(O2), .in3(O3), .in4(O4), .in5(O5), .in6(O6), .in7(O7), .in8(O8), .in9(O9),
    .in10(O10), .in11(O11), .in12(O12), .in13(O13), .in14(O14), .in15(O15), .in16(O16), .in17(O17),
    .in18(O18), .in19(O19), .in20(O20), .in21(O21), .in22(O22), .in23(O23), .in24(O24), .in25(O25),
    .in26(O26), .in27(O27), .in28(O28), .in29(O29), .in30(O30), .in31(O31), .out(RD1), .sel(A1));  // open: en
  Register #(.width(32)) register_1 (.D({32{1'b0}}), .en(we), .Q(O0), .clk(clk), .clr(reset));
  Register #(.width(32)) register_2 (.D(I8), .en(we), .Q(O8), .clk(clk), .clr(reset));
  Register #(.width(32)) register_3 (.D(I16), .en(we), .Q(O16), .clk(clk), .clr(reset));
  Register #(.width(32)) register_4 (.D(I24), .en(we), .Q(O24), .clk(clk), .clr(reset));
  Register #(.width(32)) register_5 (.D(I1), .en(we), .Q(O1), .clk(clk), .clr(reset));
  Register #(.width(32)) register_6 (.D(I9), .en(we), .Q(O9), .clk(clk), .clr(reset));
  Register #(.width(32)) register_7 (.D(I17), .en(we), .Q(O17), .clk(clk), .clr(reset));
  Register #(.width(32)) register_8 (.D(I25), .en(we), .Q(O25), .clk(clk), .clr(reset));
  Register #(.width(32)) register_9 (.D(I2), .en(we), .Q(O2), .clk(clk), .clr(reset));
  Register #(.width(32)) register_10 (.D(I10), .en(we), .Q(O10), .clk(clk), .clr(reset));
  Register #(.width(32)) register_11 (.D(I18), .en(we), .Q(O18), .clk(clk), .clr(reset));
  Register #(.width(32)) register_12 (.D(I26), .en(we), .Q(O26), .clk(clk), .clr(reset));
  Register #(.width(32)) register_13 (.D(I3), .en(we), .Q(O3), .clk(clk), .clr(reset));
  Register #(.width(32)) register_14 (.D(I11), .en(we), .Q(O11), .clk(clk), .clr(reset));
  Register #(.width(32)) register_15 (.D(I19), .en(we), .Q(O19), .clk(clk), .clr(reset));
  Register #(.width(32)) register_16 (.D(I27), .en(we), .Q(O27), .clk(clk), .clr(reset));
  Register #(.width(32)) register_17 (.D(I4), .en(we), .Q(O4), .clk(clk), .clr(reset));
  Register #(.width(32)) register_18 (.D(I12), .en(we), .Q(O12), .clk(clk), .clr(reset));
  Register #(.width(32)) register_19 (.D(I20), .en(we), .Q(O20), .clk(clk), .clr(reset));
  Register #(.width(32)) register_20 (.D(I28), .en(we), .Q(O28), .clk(clk), .clr(reset));
  Register #(.width(32)) register_21 (.D(I5), .en(we), .Q(O5), .clk(clk), .clr(reset));
  Register #(.width(32)) register_22 (.D(I13), .en(we), .Q(O13), .clk(clk), .clr(reset));
  Register #(.width(32)) register_23 (.D(I21), .en(we), .Q(O21), .clk(clk), .clr(reset));
  Register #(.width(32)) register_24 (.D(I29), .en(we), .Q(O29), .clk(clk), .clr(reset));
  Register #(.width(32)) register_25 (.D(I6), .en(we), .Q(O6), .clk(clk), .clr(reset));
  Register #(.width(32)) register_26 (.D(I14), .en(we), .Q(O14), .clk(clk), .clr(reset));
  Register #(.width(32)) register_27 (.D(I22), .en(we), .Q(O22), .clk(clk), .clr(reset));
  Register #(.width(32)) register_28 (.D(I30), .en(we), .Q(O30), .clk(clk), .clr(reset));
  Register #(.width(32)) register_29 (.D(I7), .en(we), .Q(O7), .clk(clk), .clr(reset));
  Register #(.width(32)) register_30 (.D(I15), .en(we), .Q(O15), .clk(clk), .clr(reset));
  Register #(.width(32)) register_31 (.D(I23), .en(we), .Q(O23), .clk(clk), .clr(reset));
  Register #(.width(32)) register_32 (.D(I31), .en(we), .Q(O31), .clk(clk), .clr(reset));
endmodule

module IM (
  input  [31:0] in_1,
  output [31:0] out_2
);

  wire [31:0] subtractor_1_out;

  Subtractor #(.width(32)) subtractor_1 (.a(in_1), .b(32'h3000), .out(subtractor_1_out));  // open: bin, bout
  ROM #(.addrWidth(5), .dataWidth(32)) rom_1 (.addr(subtractor_1_out[6:2]), .data(out_2));  // open: sel
endmodule

module Controller (
  input  [5:0] Op,
  input  [5:0] funct,
  output [1:0] control,
  output ALUsrc,
  output MemWrite,
  output MemtoReg,
  output RegWrite,
  output [3:0] out_8,
  output RegDst,
  output ESTop
);

  wire addiu, addu, beq, comparator_7_eq, comparator_8_eq, comparator_9_eq, j, lw, ori,
       priority_encoder_1_gs, subu, sw;
  wire [3:0] priority_encoder_1_out;

  Comparator #(.width(6)) comparator_1 (.a(Op), .b(6'b100011), .eq(lw));  // open: gt, lt
  Comparator #(.width(6)) comparator_2 (.a(Op), .b(6'b101011), .eq(sw));  // open: gt, lt
  Comparator #(.width(6)) comparator_3 (.a(Op), .b(6'b000100), .eq(beq));  // open: gt, lt
  Comparator #(.width(6)) comparator_4 (.a(Op), .b(6'b000010), .eq(j));  // open: gt, lt
  Comparator #(.width(6)) comparator_5 (.a(Op), .b(6'b001101), .eq(ori));  // open: gt, lt
  Comparator #(.width(6)) comparator_6 (.a(Op), .b(6'b001001), .eq(addiu));  // open: gt, lt
  Comparator #(.width(6)) comparator_7 (.a(Op), .b({6{1'b0}}), .eq(comparator_7_eq));  // open: gt, lt
  Comparator #(.width(6)) comparator_8 (.a(funct), .b(6'b100001), .eq(comparator_8_eq));  // open: gt, lt
  Comparator #(.width(6)) comparator_9 (.a(funct), .b(6'b100011), .eq(comparator_9_eq));  // open: gt, lt
  and and_1 (addu, comparator_8_eq, comparator_7_eq);
  and and_2 (subu, comparator_9_eq, comparator_7_eq);
  Priority_Encoder #(.select(4)) priority_encoder_1 (
    .in0(addu), .in1(subu), .in2(lw), .in3(sw), .in4(ori), .in5(beq), .in6(j), .in7(addiu),
    .out(priority_encoder_1_out), .gs(priority_encoder_1_gs));  // open: in8, in9, in10, in11, in12, in13, in14, in15, en_out, en_in
  Multiplexer #(.width(4), .enable("false")) multiplexer_1 (
    .in0(4'b0000), .in1(priority_encoder_1_out), .out(out_8), .sel(priority_encoder_1_gs));
  Multiplexer #(.select(4), .width(2), .enable("false")) multiplexer_2 (
    .in0(2'b00), .in1(2'b00), .in2(2'b00), .in3(2'b00), .in4(2'b00), .in5(2'b11), .in6(2'b01), .out(control),
    .sel(out_8));  // open: in7, in8, in9, in10, in11, in12, in13, in14, in15
  Multiplexer #(.select(4), .enable("false")) multiplexer_3 (
    .in0(1'b1), .in1(1'b1), .in2(1'b1), .in3(1'b0), .in4(1'b1), .in5(1'b0), .in6(1'b0), .out(RegWrite),
    .sel(out_8));  // open: in7, in8, in9, in10, in11, in12, in13, in14, in15
  Multiplexer #(.select(4), .enable("false")) multiplexer_4 (
    .in0(1'b0), .in1(1'b0), .in2(1'b0), .in3(1'b1), .in4(1'b0), .in5(1'b0), .in6(1'b0), .out(MemWrite),
    .sel(out_8));  // open: in7, in8, in9, in10, in11, in12, in13, in14, in15
  Multiplexer #(.select(4), .enable("false")) multiplexer_5 (
    .in0(1'b1), .in1(1'b1), .in2(1'b0), .in3(1'b0), .in4(1'b0), .in5(1'b0), .in6(1'b0), .out(RegDst),
    .sel(out_8));  // open: in7, in8, in9, in10, in11, in12, in13, in14, in15
  Multiplexer #(.select(4), .enable("false")) multiplexer_6 (
    .in0(1'b0), .in1(1'b0), .in2(1'b1), .in3(1'b1), .in4(1'b1), .in5(1'b0), .in6(1'b0), .out(ALUsrc),
    .sel(out_8));  // open: in7, in8, in9, in10, in11, in12, in13, in14, in15
  Multiplexer #(.select(4), .enable("false")) multiplexer_7 (
    .in0(1'b0), .in1(1'b0), .in2(1'b1), .in3(1'b1), .in4(1'b0), .in5(1'b0), .in6(1'b0), .out(ESTop),
    .sel(out_8));  // open: in7, in8, in9, in10, in11, in12, in13, in14, in15
  Multiplexer #(.select(4), .enable("false")) multiplexer_8 (
    .in0(1'b0), .in1(1'b0), .in2(1'b1), .in3(1'b0), .in4(1'b0), .in5(1'b0), .in6(1'b0), .out(MemtoReg),
    .sel(out_8));  // open: in7, in8, in9, in10, in11, in12, in13, in14, in15
endmodule

module DM (
  input  [31:0] in_1,
  input  [31:0] in_2,
  input  WE,
  input  CLK,
  input  in_5,
  output [31:0] out_6
);

  RAM #(.addrWidth(16), .dataWidth(32), .bus("separate")) ram_1 (
    .addr(in_1[17:2]), .din(in_2), .data(out_6), .str(WE), .clk(CLK), .clr(in_5));  // open: sel, ld
endmodule

module EXT (
  input  [15:0] in_1,
  input  in_2,
  output [31:0] out_3
);

  wire [31:0] bit_extender_1_out, bit_extender_2_out;

  assign bit_extender_1_out = {{16{1'b0}}, in_1};  // Bit_Extender bit_extender_1
  assign bit_extender_2_out = {{16{in_1[15]}}, in_1};  // Bit_Extender bit_extender_2
  Multiplexer #(.width(32), .enable("false")) multiplexer_1 (
    .in0(bit_extender_1_out), .in1(bit_extender_2_out), .out(out_3), .sel(in_2));
endmodule
