// Logisim project cpu_own.circ as structural Verilog: 12 circuits, main circuit main
module main (
  input  reset,
  output [31:0] out_2,
  output out_3,
  output [4:0] out_4,
  output [31:0] out_5,
  output out_6,
  output [4:0] out_7,
  output [31:0] out_8
);

  wire ALUsrc, clk, controller_1_shiftsrc, EXTop, MemtoReg, PCtoReg, RegDst, Regra, zero;
  wire [1:0] NPC_Sel;
  wire [3:0] ALUop;
  wire [4:0] multiplexer_2_out, multiplexer_6_out, splliter_1__6_10, splliter_1_rd_11_15,
       splliter_1_rs_21_25, splliter_1_rt_16_20;
  wire [5:0] splliter_1_funct, splliter_1_opcpde;
  wire [15:0] imm16;
  wire [25:0] imm26;
  wire [31:0] dm_1_data, ext_1_extout, GRF, Memaddr, multiplexer_1_out, multiplexer_5_out, npc_1_npc,
       pc_1_pc, PCplus4;

  Clock u_clk (.out(clk));
  NPC npc_1 (.NPC(npc_1_npc), .PC(pc_1_pc), .Imm26(imm26), .GRF(GRF), .Imm16(imm16), .control(NPC_Sel), .zero(zero));
  PC pc_1 (.NPC(npc_1_npc), .clk(clk), .reset(reset), .PC(pc_1_pc));
  Adder #(.width(32)) adder_1 (.a(32'h4), .b(pc_1_pc), .out(PCplus4));  // open: cin, cout
  IM im_1 (.in_1(pc_1_pc), .out_2(out_2));
  splliter splliter_1 (
    .Instr(out_2), .imm26(imm26), .OPcpde(splliter_1_opcpde), .funct(splliter_1_funct),
    .Rs_21_25(splliter_1_rs_21_25), .Rt_16_20(splliter_1_rt_16_20), .Rd_11_15(splliter_1_rd_11_15),
    .imm16(imm16), ._6_10(splliter_1__6_10));
  Multiplexer #(.width(32)) multiplexer_1 (
    .in0({Memaddr[31:7], out_7, Memaddr[1:0]}), .in1(dm_1_data), .out(multiplexer_1_out), .sel(MemtoReg));  // open: en
  Multiplexer #(.width(5)) multiplexer_2 (
    .in0(splliter_1_rt_16_20), .in1(splliter_1_rd_11_15), .out(multiplexer_2_out), .sel(RegDst));  // open: en
  Multiplexer #(.width(32)) multiplexer_3 (
    .in0(multiplexer_1_out), .in1(PCplus4), .out(out_5), .sel(PCtoReg));  // open: en
  Multiplexer #(.width(5)) multiplexer_4 (
    .in0(multiplexer_2_out), .in1({5{1'b1}}), .out(out_4), .sel(Regra));  // open: en
  EXT ext_1 (.imm16(imm16), .EXTop(EXTop), .EXTout(ext_1_extout));
  GRF grf_1 (
    .A1(splliter_1_rs_21_25), .A2(splliter_1_rt_16_20), .A3(out_4), .WD(out_5), .RD1(GRF), .RD2(out_8),
    .clk(clk), .reset(reset), .we(out_3));
  Controller controller_1 (
    .opcode(splliter_1_opcpde), .funct(splliter_1_funct), .NPC_Sel(NPC_Sel), .ALUop(ALUop), .RegWrite(out_3),
    .EXTop(EXTop), .ALUSrc(ALUsrc), .RegDst(RegDst), .MemWrite(out_6), .MemtoReg(MemtoReg),
    .PCtoReg(PCtoReg), .Regra(Regra), .ShiftSrc(controller_1_shiftsrc));
  Multiplexer #(.width(32)) multiplexer_5 (
    .in0(out_8), .in1(ext_1_extout), .out(multiplexer_5_out), .sel(ALUsrc));  // open: en
  Multiplexer #(.width(5)) multiplexer_6 (
    .in0(splliter_1__6_10), .in1(GRF[4:0]), .out(multiplexer_6_out), .sel(controller_1_shiftsrc));  // open: en
  ALU alu_1 (
    .inputA(GRF), .inputB(multiplexer_5_out), .ALUop(ALUop), .outputA({Memaddr[31:7], out_7, Memaddr[1:0]}),
    .zero(zero), .shift(multiplexer_6_out));
  DM dm_1 (
    .Addr({Memaddr[31:7], out_7, Memaddr[1:0]}), .WD(out_8), .Data(dm_1_data), .WE(out_6), .clk(clk),
    .reset(reset));

  // Other names for the same wires on the sheet: instr[31:0] = out_2; Memaddr[6:2] = out_7; Memdata[31:0] = out_8;
  //   MemWrite = out_6; Regaddr[4:0] = out_4; Regdata[31:0] = out_5; RegWrite = out_3
endmodule

module PC (
  input  [31:0] NPC,
  input  clk,
  input  reset,
  output [31:0] PC
);

  wire [31:0] register_1_q, xor_1_out;

  assign xor_1_out = 32'h3000 ^ NPC;  // XOR_Gate xor_1, 32 bits wide
  Register #(.width(32)) register_1 (.D(xor_1_out), .Q(register_1_q), .clk(clk), .clr(reset));  // open: en
  assign PC = 32'h3000 ^ register_1_q;  // XOR_Gate xor_2, 32 bits wide
endmodule

module NPC (
  input  [31:0] PC,
  input  [25:0] Imm26,
  input  [31:0] GRF,
  input  [15:0] Imm16,
  input  [1:0] control,
  input  zero,
  output [31:0] NPC
);

  wire [31:0] adder_1_out, adder_2_out, bit_extender_1_out, multiplexer_1_out;

  Adder #(.width(32)) adder_1 (.a(32'h4), .b(PC), .out(adder_1_out));  // open: cin, cout
  assign bit_extender_1_out = {{14{Imm16[15]}}, {Imm16, 2'b00}};  // Bit_Extender bit_extender_1
  Adder #(.width(32)) adder_2 (.a(adder_1_out), .b(bit_extender_1_out), .out(adder_2_out));  // open: cin, cout
  Multiplexer #(.width(32), .enable("false")) multiplexer_1 (
    .in0(adder_1_out), .in1(adder_2_out), .out(multiplexer_1_out), .sel(zero));
  Multiplexer #(.select(2), .width(32), .enable("false")) multiplexer_2 (
    .in0(adder_1_out), .in1({PC[31:28], Imm26, 2'b00}), .in2(GRF), .in3(multiplexer_1_out), .out(NPC),
    .sel(control));
endmodule

module IM (
  input  [31:0] in_1,
  output [31:0] out_2
);

  wire [31:0] subtractor_1_out;

  Subtractor #(.width(32)) subtractor_1 (.a(in_1), .b(32'h3000), .out(subtractor_1_out));  // open: bin, bout
  ROM #(.addrWidth(16), .dataWidth(32)) rom_1 (.addr(subtractor_1_out[17:2]), .data(out_2));  // open: sel
endmodule

module DM (
  input  [31:0] Addr,
  input  WE,
  input  clk,
  input  reset,
  input  [31:0] WD,
  output [31:0] Data
);

  RAM #(.addrWidth(16), .dataWidth(32), .bus("separate")) ram_1 (
    .addr(Addr[17:2]), .din(WD), .data(Data), .str(WE), .clk(clk), .clr(reset));  // open: sel, ld
endmodule

module GRF (
  input  [4:0] A1,
  input  clk,
  input  reset,
  input  we,
  input  [4:0] A2,
  input  [4:0] A3,
  input  [31:0] WD,
  output [31:0] RD1,
  output [31:0] RD2
);

  wire [31:0] I0, I1, I2, I3, I4, I5, I6, I7, I8, I9, I10, I11, I12, I13, I14, I15, I16, I17, I18, I19, I20,
       I21, I22, I23, I24, I25, I26, I27, I28, I29, I30, I31, O0, O1, O2, O3, O4, O5, O6, O7, O8, O9, O10,
       O11, O12, O13, O14, O15, O16, O17, O18, O19, O20, O21, O22, O23, O24, O25, O26, O27, O28, O29, O30,
       O31;

  Demultiplexer #(.select(5), .width(32), .tristate("true")) demultiplexer_1 (
    .out0(I0), .out1(I1), .out2(I2), .out3(I3), .out4(I4), .out5(I5), .out6(I6), .out7(I7), .out8(I8),
    .out9(I9), .out10(I10), .out11(I11), .out12(I12), .out13(I13), .out14(I14), .out15(I15), .out16(I16),
    .out17(I17), .out18(I18), .out19(I19), .out20(I20), .out21(I21), .out22(I22), .out23(I23), .out24(I24),
    .out25(I25), .out26(I26), .out27(I27), .out28(I28), .out29(I29), .out30(I30), .out31(I31), .in(WD),
    .sel(A3));  // open: en
  Multiplexer #(.select(5), .width(32)) multiplexer_1 (
    .in0(O0), .in1(O1), .in2(O2), .in3(O3), .in4(O4), .in5(O5), .in6(O6), .in7(O7), .in8(O8), .in9(O9),
    .in10(O10), .in11(O11), .in12(O12), .in13(O13), .in14(O14), .in15(O15), .in16(O16), .in17(O17),
    .in18(O18), .in19(O19), .in20(O20), .in21(O21), .in22(O22), .in23(O23), .in24(O24), .in25(O25),
    .in26(O26), .in27(O27), .in28(O28), .in29(O29), .in30(O30), .in31(O31), .out(RD2), .sel(A2));  // open: en
  Multiplexer #(.select(5), .width(32)) multiplexer_2 (
    .in0(O0), .in1(O1), .in2(O2), .in3(O3), .in4(O4), .in5(O5), .in6(O6), .in7(O7), .in8(O8), .in9(O9),
    .in10(O10), .in11(O11), .in12(O12), .in13(O13), .in14(O14), .in15(O15), .in16(O16), .in17(O17),
    .in18(O18), .in19(O19), .in20(O20), .in21(O21), .in22(O22), .in23(O23), .in24(O24), .in25(O25),
    .in26(O26), .in27(O27), .in28(O28), .in29(O29), .in30(O30), .in31(O31), .out(RD1), .sel(A1));  // open: en
  Register #(.width(32)) register_1 (.D({32{1'b0}}), .en(we), .Q(O0), .clk(clk), .clr(reset));
  Register #(.width(32)) register_2 (.D(I8), .en(we), .Q(O8), .clk(clk), .clr(reset));
  Register #(.width(32)) register_3 (.D(I16), .en(we), .Q(O16), .clk(clk), .clr(reset));
  Register #(.width(32)) register_4 (.D(I24), .en(we), .Q(O24), .clk(clk), .clr(reset));
  Register #(.width(32)) register_5 (.D(I1), .en(we), .Q(O1), .clk(clk), .clr(reset));
  Register #(.width(32)) register_6 (.D(I9), .en(we), .Q(O9), .clk(clk), .clr(reset));
  Register #(.width(32)) register_7 (.D(I17), .en(we), .Q(O17), .clk(clk), .clr(reset));
  Register #(.width(32)) register_8 (.D(I25), .en(we), .Q(O25), .clk(clk), .clr(reset));
  Register #(.width(32)) register_9 (.D(I2), .en(we), .Q(O2), .clk(clk), .clr(reset));
  Register #(.width(32)) register_10 (.D(I10), .en(we), .Q(O10), .clk(clk), .clr(reset));
  Register #(.width(32)) register_11 (.D(I18), .en(we), .Q(O18), .clk(clk), .clr(reset));
  Register #(.width(32)) register_12 (.D(I26), .en(we), .Q(O26), .clk(clk), .clr(reset));
  Register #(.width(32)) register_13 (.D(I3), .en(we), .Q(O3), .clk(clk), .clr(reset));
  Register #(.width(32)) register_14 (.D(I11), .en(we), .Q(O11), .clk(clk), .clr(reset));
  Register #(.width(32)) register_15 (.D(I19), .en(we), .Q(O19), .clk(clk), .clr(reset));
  Register #(.width(32)) register_16 (.D(I27), .en(we), .Q(O27), .clk(clk), .clr(reset));
  Register #(.width(32)) register_17 (.D(I4), .en(we), .Q(O4), .clk(clk), .clr(reset));
  Register #(.width(32)) register_18 (.D(I12), .en(we), .Q(O12), .clk(clk), .clr(reset));
  Register #(.width(32)) register_19 (.D(I20), .en(we), .Q(O20), .clk(clk), .clr(reset));
  Register #(.width(32)) register_20 (.D(I28), .en(we), .Q(O28), .clk(clk), .clr(reset));
  Register #(.width(32)) register_21 (.D(I5), .en(we), .Q(O5), .clk(clk), .clr(reset));
  Register #(.width(32)) register_22 (.D(I13), .en(we), .Q(O13), .clk(clk), .clr(reset));
  Register #(.width(32)) register_23 (.D(I21), .en(we), .Q(O21), .clk(clk), .clr(reset));
  Register #(.width(32)) register_24 (.D(I29), .en(we), .Q(O29), .clk(clk), .clr(reset));
  Register #(.width(32)) register_25 (.D(I6), .en(we), .Q(O6), .clk(clk), .clr(reset));
  Register #(.width(32)) register_26 (.D(I14), .en(we), .Q(O14), .clk(clk), .clr(reset));
  Register #(.width(32)) register_27 (.D(I22), .en(we), .Q(O22), .clk(clk), .clr(reset));
  Register #(.width(32)) register_28 (.D(I30), .en(we), .Q(O30), .clk(clk), .clr(reset));
  Register #(.width(32)) register_29 (.D(I7), .en(we), .Q(O7), .clk(clk), .clr(reset));
  Register #(.width(32)) register_30 (.D(I15), .en(we), .Q(O15), .clk(clk), .clr(reset));
  Register #(.width(32)) register_31 (.D(I23), .en(we), .Q(O23), .clk(clk), .clr(reset));
  Register #(.width(32)) register_32 (.D(I31), .en(we), .Q(O31), .clk(clk), .clr(reset));
endmodule

module splliter (
  input  [31:0] Instr,
  output [25:0] imm26,
  output [4:0] _6_10,
  output [5:0] OPcpde,
  output [5:0] funct,
  output [4:0] Rs_21_25,
  output [4:0] Rt_16_20,
  output [4:0] Rd_11_15,
  output [15:0] imm16
);


  assign _6_10 = Instr[10:6];
  assign funct = Instr[5:0];
  assign imm16 = Instr[15:0];
  assign imm26 = Instr[25:0];
  assign OPcpde = Instr[31:26];
  assign Rd_11_15 = Instr[15:11];
  assign Rs_21_25 = Instr[25:21];
  assign Rt_16_20 = Instr[20:16];
endmodule

module EXT (
  input  [15:0] imm16,
  input  EXTop,
  output [31:0] EXTout
);

  wire [31:0] bit_extender_1_out, bit_extender_2_out;

  assign bit_extender_1_out = {{16{1'b0}}, imm16};  // Bit_Extender bit_extender_1
  assign bit_extender_2_out = {{16{imm16[15]}}, imm16};  // Bit_Extender bit_extender_2
  Multiplexer #(.width(32), .enable("false")) multiplexer_1 (
    .in0(bit_extender_1_out), .in1(bit_extender_2_out), .out(EXTout), .sel(EXTop));
endmodule

module ALU (
  input  [31:0] inputA,
  input  [31:0] inputB,
  input  [3:0] ALUop,
  input  [4:0] shift,
  output [31:0] outputA,
  output zero
);

  wire AequalsB, AnotequalsB, comparator_3_eq;
  wire [0:0] AcompareB;
  wire [31:0] AorB, AplusB, AsubB, AxorB, Bleftshift, Bleftshift16;

  Comparator #(.width(32)) comparator_1 (.a(inputA), .b(inputB), .eq(AcompareB[0]));  // open: gt, lt
  Adder #(.width(32)) adder_1 (.a(inputA), .b(inputB), .out(AplusB));  // open: cin, cout
  Subtractor #(.width(32)) subtractor_1 (.a(inputA), .b(inputB), .out(AsubB));  // open: bin, bout
  Shifter #(.width(32)) shifter_1 (.in(inputB), .\dist (5'b10000), .out(Bleftshift16));
  Comparator #(.width(32)) comparator_2 (.a(inputA), .b(inputB), .eq(AequalsB));  // open: gt, lt
  Comparator #(.width(32)) comparator_3 (.a(inputA), .b(inputB), .eq(comparator_3_eq));  // open: gt, lt
  assign AorB = inputA | inputB;  // OR_Gate or_1, 32 bits wide
  Shifter #(.width(32)) shifter_2 (.in(inputB), .\dist (shift), .out(Bleftshift));
  assign AxorB = inputA ^ inputB;  // XOR_Gate xor_1, 32 bits wide
  not not_1 (AnotequalsB, comparator_3_eq);
  Multiplexer #(.select(4), .width(32)) multiplexer_1 (
    .in0(AplusB), .in1(AsubB), .in2(AorB), .in3(AxorB), .in4(Bleftshift16), .in8(Bleftshift),
    .in11({{31{1'b0}}, AcompareB[0]}), .out(outputA), .sel(ALUop));  // open: in5, in6, in7, in9, in10, in12, in13, in14, in15, en
  Multiplexer #(.select(4)) multiplexer_2 (
    .in14(AnotequalsB), .in15(AequalsB), .out(zero), .sel(ALUop));  // open: in0, in1, in2, in3, in4, in5, in6, in7, in8, in9, in10, in11, in12, in13, en
endmodule

module Controller (
  input  [5:0] opcode,
  input  [5:0] funct,
  output [1:0] NPC_Sel,
  output [3:0] ALUop,
  output RegWrite,
  output EXTop,
  output ALUSrc,
  output RegDst,
  output MemWrite,
  output MemtoReg,
  output PCtoReg,
  output Regra,
  output ShiftSrc
);

  wire addi, addiu, addu, \and , beq, blez, bne, comparator_1_eq, comparator_2_eq, comparator_3_eq,
       comparator_4_eq, comparator_5_eq, comparator_6_eq, comparator_7_eq, comparator_8_eq, comparator_9_eq,
       j, jalr, jr, lb, lh, lui, lw, \or , or_1_out, or_2_out, or_3_out, or_4_out, or_5_out, or_6_out,
       or_7_out, or_8_out, or_9_out, or_10_out, ori, R, sb, sh, sll, slt, slti, subu, sw, xori;

  Comparator #(.width(6)) comparator_1 (.a(funct), .b(6'b100001), .eq(comparator_1_eq));  // open: gt, lt
  Comparator #(.width(6)) comparator_2 (.a(funct), .b(6'b100011), .eq(comparator_2_eq));  // open: gt, lt
  Comparator #(.width(6)) comparator_3 (.a(funct), .b(6'b100100), .eq(comparator_3_eq));  // open: gt, lt
  Comparator #(.width(6)) comparator_4 (.a(funct), .b(6'b100101), .eq(comparator_4_eq));  // open: gt, lt
  Comparator #(.width(6)) comparator_5 (.a(funct), .b({6{1'b0}}), .eq(comparator_5_eq));  // open: gt, lt
  Comparator #(.width(6)) comparator_6 (.a(funct), .b(6'b000100), .eq(comparator_6_eq));  // open: gt, lt
  Comparator #(.width(6)) comparator_7 (.a(funct), .b(6'b101010), .eq(comparator_7_eq));  // open: gt, lt
  Comparator #(.width(6)) comparator_8 (.a(funct), .b(6'b001000), .eq(comparator_8_eq));  // open: gt, lt
  Comparator #(.width(6)) comparator_9 (.a(funct), .b(6'b001001), .eq(comparator_9_eq));  // open: gt, lt
  and and_1 (addu, comparator_1_eq, R);
  and and_2 (subu, comparator_2_eq, R);
  and and_3 (\and , comparator_3_eq, R);
  and and_4 (\or , comparator_4_eq, R);
  and and_5 (sll, comparator_5_eq, R);
  and and_6 (ShiftSrc, comparator_6_eq, R);
  and and_7 (slt, comparator_7_eq, R);
  and and_8 (jr, comparator_8_eq, R);
  and and_9 (jalr, comparator_9_eq, R);
  Comparator #(.width(6)) comparator_10 (.a(opcode), .b({6{1'b0}}), .eq(R));  // open: gt, lt
  Comparator #(.width(6)) comparator_11 (.a(opcode), .b(6'b100011), .eq(lw));  // open: gt, lt
  Comparator #(.width(6)) comparator_12 (.a(opcode), .b(6'b101011), .eq(sw));  // open: gt, lt
  Comparator #(.width(6)) comparator_13 (.a(opcode), .b(6'b001000), .eq(addi));  // open: gt, lt
  Comparator #(.width(6)) comparator_14 (.a(opcode), .b(6'b001101), .eq(ori));  // open: gt, lt
  Comparator #(.width(6)) comparator_15 (.a(opcode), .b(6'b001111), .eq(lui));  // open: gt, lt
  Comparator #(.width(6)) comparator_16 (.a(opcode), .b(6'b001010), .eq(slti));  // open: gt, lt
  Comparator #(.width(6)) comparator_17 (.a(opcode), .b(6'b101000), .eq(sb));  // open: gt, lt
  Comparator #(.width(6)) comparator_18 (.a(opcode), .b(6'b101001), .eq(sh));  // open: gt, lt
  Comparator #(.width(6)) comparator_19 (.a(opcode), .b(6'b100001), .eq(lh));  // open: gt, lt
  Comparator #(.width(6)) comparator_20 (.a(opcode), .b(6'b100000), .eq(lb));  // open: gt, lt
  Comparator #(.width(6)) comparator_21 (.a(opcode), .b(6'b001001), .eq(addiu));  // open: gt, lt
  Comparator #(.width(6)) comparator_22 (.a(opcode), .b(6'b000100), .eq(beq));  // open: gt, lt
  Comparator #(.width(6)) comparator_23 (.a(opcode), .b(6'b000010), .eq(j));  // open: gt, lt
  Comparator #(.width(6)) comparator_24 (.a(opcode), .b(6'b000110), .eq(blez));  // open: gt, lt
  Comparator #(.width(6)) comparator_25 (.a(opcode), .b(6'b000011), .eq(Regra));  // open: gt, lt
  Comparator #(.width(6)) comparator_26 (.a(opcode), .b(6'b001110), .eq(xori));  // open: gt, lt
  Comparator #(.width(6)) comparator_27 (.a(opcode), .b(6'b000101), .eq(bne));  // open: gt, lt
  Comparator #(.width(6)) comparator_28 (.a(opcode), .b(6'b001010), .eq(slti));  // open: gt, lt
  or or_1 (or_1_out, slti, slt);
  or or_2 (or_2_out, j, Regra);
  or or_3 (or_3_out, jr, jalr);
  or or_4 (or_4_out, bne, beq);
  or or_5 (or_5_out, sll, ShiftSrc);
  or or_6 (or_6_out, sw, sb, sh);
  or or_7 (or_7_out, beq, bne, blez);
  or or_8 (or_8_out, lw, lb, lh);
  or or_9 (or_9_out, sw, sb, sh);
  or or_10 (or_10_out, lw, lb, lh);
  Priority_Encoder #(.select(2)) priority_encoder_1 (
    .in1(or_2_out), .in2(or_3_out), .in3(or_4_out), .out(NPC_Sel));  // open: in0, gs, en_out, en_in
  Pull_Resistor pull_resistor_1 (.node(ALUop));
  Priority_Encoder #(.select(4)) priority_encoder_2 (
    .in1(subu), .in2(ori), .in3(xori), .in4(lui), .in8(or_5_out), .in11(or_1_out), .in14(bne), .in15(beq),
    .out(ALUop));  // open: in0, in5, in6, in7, in9, in10, in12, in13, gs, en_out, en_in
  nor nor_1 (RegWrite, sw, sb, sh, jr, j, beq, bne, blez);
  or or_11 (EXTop, or_6_out, addi, addiu, or_7_out, slti, or_8_out);
  or or_12 (ALUSrc, or_9_out, addi, addiu, ori, xori, slti, or_10_out);
  or or_13 (RegDst, addu, subu, \and , \or , slt, sll, ShiftSrc, jalr);
  or or_14 (MemWrite, sw, sb, sh);
  or or_15 (MemtoReg, lw, lb, lh);
  or or_16 (PCtoReg, Regra, jalr);
  Pull_Resistor pull_resistor_2 (.node(NPC_Sel));

  // Other names for the same wires on the sheet: jal = Regra; op[5:0] = opcode; sllv = ShiftSrc
endmodule

module ALU2 (
  input  [31:0] inputA,
  input  [31:0] inputB,
  input  [3:0] \type ,
  output [31:0] outputA,
  output zero
);

  wire AequalsB, AnotequalsB, comparator_2_eq;
  wire [31:0] AorB, AplusB, AsubB, Bleftshift16;

  Adder #(.width(32)) adder_1 (.a(inputA), .b(inputB), .out(AplusB));  // open: cin, cout
  Subtractor #(.width(32)) subtractor_1 (.a(inputA), .b(inputB), .out(AsubB));  // open: bin, bout
  assign AorB = inputA | inputB;  // OR_Gate or_1, 32 bits wide
  Shifter #(.width(32)) shifter_1 (.in(inputA), .\dist (5'b10000), .out(Bleftshift16));
  Comparator #(.width(32)) comparator_1 (.a(inputA), .b(inputB), .eq(AequalsB));  // open: gt, lt
  not not_1 (AnotequalsB, comparator_2_eq);
  Comparator #(.width(32)) comparator_2 (.a(inputA), .b(inputB), .eq(comparator_2_eq));  // open: gt, lt
  Multiplexer #(.select(4), .width(32)) multiplexer_1 (
    .in1(AplusB), .in2(AsubB), .in3(AplusB), .in4(AorB), .in5(Bleftshift16), .in6(AplusB), .in7(AplusB),
    .out(outputA), .sel(\type ));  // open: in0, in8, in9, in10, in11, in12, in13, in14, in15, en
  Multiplexer #(.select(4)) multiplexer_2 (
    .in8(AequalsB), .in9(AnotequalsB), .out(zero), .sel(\type ));  // open: in0, in1, in2, in3, in4, in5, in6, in7, in10, in11, in12, in13, in14, in15, en
endmodule

module Controller2 (
  input  [5:0] opcode,
  input  [5:0] funct,
  output [1:0] NPC_Sel,
  output RegWrite,
  output EXTop,
  output ALUsrc,
  output [3:0] \type ,
  output RegDst,
  output MemWrite,
  output MemtoReg,
  output PCtoReg,
  output Regra
);

  wire addi, addiu, addu, \and , beq, blez, bne, comparator_1_eq, comparator_2_eq, comparator_3_eq,
       comparator_4_eq, comparator_5_eq, comparator_6_eq, comparator_7_eq, comparator_8_eq, comparator_9_eq,
       j, jal, jalr, jr, lb, lh, lui, lw, \or , ori, priority_encoder_1_gs, R, sb, sh, sll, sllv, slt, slti,
       subu, sw, xori;
  wire [3:0] priority_encoder_1_out;

  Priority_Encoder #(.select(4)) priority_encoder_1 (
    .in1(addu), .in2(subu), .in3(addiu), .in4(ori), .in5(lui), .in6(lw), .in7(sw), .in8(beq), .in9(bne),
    .in10(j), .in11(jal), .in12(jr), .in13(jalr), .out(priority_encoder_1_out), .gs(priority_encoder_1_gs));  // open: in0, in14, in15, en_out, en_in
  Comparator #(.width(6)) comparator_1 (.a(funct), .b(6'b100001), .eq(comparator_1_eq));  // open: gt, lt
  Multiplexer #(.width(4), .enable("false")) multiplexer_1 (
    .in0(4'b0000), .in1(priority_encoder_1_out), .out(\type ), .sel(priority_encoder_1_gs));
  and and_1 (addu, comparator_1_eq, R);
  Comparator #(.width(6)) comparator_2 (.a(funct), .b(6'b100011), .eq(comparator_2_eq));  // open: gt, lt
  and and_2 (subu, comparator_2_eq, R);
  Comparator #(.width(6)) comparator_3 (.a(funct), .b(6'b100100), .eq(comparator_3_eq));  // open: gt, lt
  and and_3 (\and , comparator_3_eq, R);
  Comparator #(.width(6)) comparator_4 (.a(funct), .b(6'b100101), .eq(comparator_4_eq));  // open: gt, lt
  and and_4 (\or , comparator_4_eq, R);
  Comparator #(.width(6)) comparator_5 (.a(funct), .b({6{1'b0}}), .eq(comparator_5_eq));  // open: gt, lt
  and and_5 (sll, comparator_5_eq, R);
  Comparator #(.width(6)) comparator_6 (.a(funct), .b(6'b000100), .eq(comparator_6_eq));  // open: gt, lt
  and and_6 (sllv, comparator_6_eq, R);
  Comparator #(.width(6)) comparator_7 (.a(funct), .b(6'b101010), .eq(comparator_7_eq));  // open: gt, lt
  and and_7 (slt, comparator_7_eq, R);
  Comparator #(.width(6)) comparator_8 (.a(funct), .b(6'b001000), .eq(comparator_8_eq));  // open: gt, lt
  and and_8 (jr, comparator_8_eq, R);
  Comparator #(.width(6)) comparator_9 (.a(funct), .b(6'b001001), .eq(comparator_9_eq));  // open: gt, lt
  and and_9 (jalr, comparator_9_eq, R);
  Multiplexer #(.select(4), .width(2)) multiplexer_2 (
    .in0(2'b00), .in1(2'b00), .in2(2'b00), .in3(2'b00), .in4(2'b00), .in5(2'b00), .in6(2'b00), .in7(2'b00),
    .in8(2'b11), .in9(2'b11), .in10(2'b01), .in11(2'b01), .in12(2'b10), .in13(2'b10), .out(NPC_Sel),
    .sel(\type ));  // open: in14, in15, en
  Multiplexer #(.select(4)) multiplexer_3 (
    .in0(1'b0), .in1(1'b1), .in2(1'b1), .in3(1'b0), .in4(1'b0), .in5(1'b0), .in6(1'b0), .in7(1'b0),
    .in8(1'b0), .in9(1'b0), .in10(1'b0), .in11(1'b0), .in12(1'b0), .in13(1'b1), .out(RegDst), .sel(\type ));  // open: in14, in15, en
  Comparator #(.width(6)) comparator_10 (.a(opcode), .b({6{1'b0}}), .eq(R));  // open: gt, lt
  Comparator #(.width(6)) comparator_11 (.a(opcode), .b(6'b100011), .eq(lw));  // open: gt, lt
  Comparator #(.width(6)) comparator_12 (.a(opcode), .b(6'b101011), .eq(sw));  // open: gt, lt
  Comparator #(.width(6)) comparator_13 (.a(opcode), .b(6'b001000), .eq(addi));  // open: gt, lt
  Comparator #(.width(6)) comparator_14 (.a(opcode), .b(6'b001101), .eq(ori));  // open: gt, lt
  Comparator #(.width(6)) comparator_15 (.a(opcode), .b(6'b001111), .eq(lui));  // open: gt, lt
  Comparator #(.width(6)) comparator_16 (.a(opcode), .b(6'b001010), .eq(slti));  // open: gt, lt
  Comparator #(.width(6)) comparator_17 (.a(opcode), .b(6'b101000), .eq(sb));  // open: gt, lt
  Comparator #(.width(6)) comparator_18 (.a(opcode), .b(6'b101001), .eq(sh));  // open: gt, lt
  Comparator #(.width(6)) comparator_19 (.a(opcode), .b(6'b100001), .eq(lh));  // open: gt, lt
  Comparator #(.width(6)) comparator_20 (.a(opcode), .b(6'b100000), .eq(lb));  // open: gt, lt
  Comparator #(.width(6)) comparator_21 (.a(opcode), .b(6'b001001), .eq(addiu));  // open: gt, lt
  Comparator #(.width(6)) comparator_22 (.a(opcode), .b(6'b000100), .eq(beq));  // open: gt, lt
  Comparator #(.width(6)) comparator_23 (.a(opcode), .b(6'b000010), .eq(j));  // open: gt, lt
  Comparator #(.width(6)) comparator_24 (.a(opcode), .b(6'b000110), .eq(blez));  // open: gt, lt
  Comparator #(.width(6)) comparator_25 (.a(opcode), .b(6'b000011), .eq(jal));  // open: gt, lt
  Comparator #(.width(6)) comparator_26 (.a(opcode), .b(6'b001110), .eq(xori));  // open: gt, lt
  Comparator #(.width(6)) comparator_27 (.a(opcode), .b(6'b000101), .eq(bne));  // open: gt, lt
  Comparator #(.width(6)) comparator_28 (.a(opcode), .b(6'b001010), .eq(slti));  // open: gt, lt
  Multiplexer #(.select(4)) multiplexer_4 (
    .in0(1'b0), .in1(1'b1), .in2(1'b1), .in3(1'b1), .in4(1'b1), .in5(1'b1), .in6(1'b1), .in7(1'b0),
    .in8(1'b0), .in9(1'b0), .in10(1'b0), .in11(1'b1), .in12(1'b0), .in13(1'b1), .out(RegWrite), .sel(\type ));  // open: in14, in15, en
  Multiplexer #(.select(4)) multiplexer_5 (
    .in0(1'b0), .in1(1'b0), .in2(1'b0), .in3(1'b0), .in4(1'b0), .in5(1'b0), .in6(1'b0), .in7(1'b1),
    .in8(1'b0), .in9(1'b0), .in10(1'b0), .in11(1'b0), .in12(1'b0), .in13(1'b0), .out(MemWrite), .sel(\type ));  // open: in14, in15, en
  Multiplexer #(.select(4)) multiplexer_6 (
    .in0(1'b0), .in1(1'b0), .in2(1'b0), .in3(1'b1), .in4(1'b0), .in5(1'b0), .in6(1'b1), .in7(1'b1),
    .in8(1'b0), .in9(1'b0), .in10(1'b0), .in11(1'b0), .in12(1'b0), .in13(1'b0), .out(EXTop), .sel(\type ));  // open: in14, in15, en
  Multiplexer #(.select(4)) multiplexer_7 (
    .in0(1'b0), .in1(1'b0), .in2(1'b0), .in3(1'b0), .in4(1'b0), .in5(1'b0), .in6(1'b1), .in7(1'b0),
    .in8(1'b0), .in9(1'b0), .in10(1'b0), .in11(1'b0), .in12(1'b0), .in13(1'b0), .out(MemtoReg), .sel(\type ));  // open: in14, in15, en
  Multiplexer #(.select(4)) multiplexer_8 (
    .in0(1'b0), .in1(1'b0), .in2(1'b0), .in3(1'b1), .in4(1'b1), .in5(1'b1), .in6(1'b1), .in7(1'b1),
    .in8(1'b0), .in9(1'b0), .in10(1'b0), .in11(1'b0), .in12(1'b0), .in13(1'b0), .out(ALUsrc), .sel(\type ));  // open: in14, in15, en
  Multiplexer #(.select(4)) multiplexer_9 (
    .in0(1'b0), .in1(1'b0), .in2(1'b0), .in3(1'b0), .in4(1'b0), .in5(1'b0), .in6(1'b0), .in7(1'b0),
    .in8(1'b0), .in9(1'b0), .in10(1'b0), .in11(1'b1), .in12(1'b0), .in13(1'b1), .out(PCtoReg), .sel(\type ));  // open: in14, in15, en
  Multiplexer #(.select(4)) multiplexer_10 (
    .in0(1'b0), .in1(1'b0), .in2(1'b0), .in3(1'b0), .in4(1'b0), .in5(1'b0), .in6(1'b0), .in7(1'b0),
    .in8(1'b0), .in9(1'b0), .in10(1'b0), .in11(1'b1), .in12(1'b0), .in13(1'b0), .out(Regra), .sel(\type ));  // open: in14, in15, en

  // Other names for the same wires on the sheet: op[5:0] = opcode
endmodule
